# Fritzing sketch Fritzing scheme 22x27 (saved by Fritzing 0.9.3b)
circuit board: 5.60158cm x 7.03054cm
perfboards: 1

parts:
  Часть1 = Arduino Nano (Rev3.0)
  PN2222A = NPN-Transistor [package="TO92 [THT]"]
  R2 = Resistor [tolerance=±5% resistance=220 package=THT]
  LED_Mode = LED - 5mm [color="Red (633nm)" package="5 mm [THT]"]
  bUp = Pushbutton [package="[THT]"]
  bDown = Pushbutton [package="[THT]"]
  R1 = Resistor [tolerance=±5% resistance=330 package=THT]
  GND = male pin header, 1 pin [form="♂ (male)"]
  IR_signal_IN = male pin header, 1 pin [form="♂ (male)"]
  J3 = male pin header, 1 pin [form="♂ (male)"]
  GND_2 = male pin header, 1 pin [form="♂ (male)"]
  Signal_OUT = male pin header, 1 pin [form="♂ (male)"]
  12v+ = male pin header, 1 pin [form="♂ (male)"]
  12v+_2 = male pin header, 1 pin [form="♂ (male)"]
  5v+ = male pin header, 1 pin [form="♂ (male)"]
  5v- = male pin header, 1 pin [form="♂ (male)"]
  12v+1 = male pin header, 1 pin [form="♂ (male)"]  # not connected
  Buzzer = Piezo Speaker

nets:
  N1: Часть1.GND, PN2222A.E, GND.pin1, GND_2.pin1
  N2: Часть1.D3, IR_signal_IN.pin1
  N3: Часть1.D5, bDown.Pin_3, bDown.Pin_4
  N4: Часть1.D6, bUp.Pin_1, bUp.Pin_2
  N5: Часть1.D8, R2.Pin_0
  N6: Часть1.D12/MISO, LED_Mode.anode
  5V: Часть1.5V, J3.pin1, 5v+.pin1
  N7: Часть1.A5, Buzzer.pin2
  N8: PN2222A.C, Signal_OUT.pin1
  N9: LED_Mode.cathode, R1.Pin_1
  N10: bUp.Pin_3, bUp.Pin_4
  N11: bDown.Pin_1, bDown.Pin_2
  N12: 12v+.pin1, 12v+_2.pin1
  N13: 5v-.pin1, Buzzer.pin1

notes:
  Д А Т Ч И К
  Земля|Сигнал|+5v
  Земля|Коммутатор|+12v
  DC-DC
  12v -> 5v
